// Logisim project example.circ as structural Verilog: 1 circuit, main circuit main
module main (
  input  reset
);

  wire and_2_out, and_3_out, clock_1_out, Keyboard_1_avail, s_r_ff_1_q, shift_register_1_p2,
       shift_register_1_p7;
  wire [6:0] Keyboard_1_data;
  wire [10:0] counter_1_q;
  wire [23:0] multiplexer_1_out;

  Clock clock_1 (.out(clock_1_out));
  Keyboard Keyboard_1 (
    .clk(clock_1_out), .re(and_3_out), .clr(reset), .avail(Keyboard_1_avail), .data(Keyboard_1_data));
  // Shift_Register shift_register_1: pin names not known; wires that end beside it: reset, shift_register_1_p2, 1'b1, clock_1_out, 1'b0, 1'b0, shift_register_1_p7
  and and_1 (shift_register_1_p2, Keyboard_1_avail, ~s_r_ff_1_q);  // AND_Gate
  S_R_Flip_Flop s_r_ff_1 (
    .S(and_2_out), .R(and_3_out), .clk(clock_1_out), .Q(s_r_ff_1_q), .reset(reset));  // open: Qn, preset
  and and_2 (and_2_out, Keyboard_1_avail, ~and_3_out);  // AND_Gate
  Counter #(.max('h7ff), .width(11)) counter_1 (
    .clr(reset), .load(1'b0), .up(1'b1), .count(s_r_ff_1_q), .clk(clock_1_out), .Q(counter_1_q));  // open: D, carry
  Multiplexer #(.width(24)) multiplexer_1 (
    .in0(24'h7f7f7f), .in1({24{1'b1}}), .out(multiplexer_1_out), .sel(shift_register_1_p7));
  and and_3 (and_3_out, counter_1_q[0], counter_1_q[1], counter_1_q[2]);
  // RGB_Video #(.cursor("No Cursor"), .width(64)) Video_8_Color_RGB_32x32_1: pin names not known; wires that end beside it: reset, clock_1_out, s_r_ff_1_q, counter_1_q[5:0], counter_1_q[10:6], multiplexer_1_out
endmodule
